# Fritzing sketch 2주차 회로도 (saved by Fritzing 0.9.3b)
breadboards: 1

parts:
  LED4 = smd LED [color="Green (570nm)" package="0603 [SMD]"]
  LED1 = smd LED [color="Yellow (595nm)" package="1206 [SMD]"]
  LED5 = smd LED [color="Orange (605nm)" package="0805 [SMD]"]
  R1 = Resistor [tolerance=±5% resistance=2.2k package=THT]
  R6 = Resistor [tolerance=±5% resistance=2.2k package=THT]
  R7 = Resistor [tolerance=±5% resistance=2.2k package=THT]
  R8 = Resistor [tolerance=±5% resistance=2.2k package=THT]
  LED6 = smd LED [color="Red (635nm)" package="0603 [SMD]"]
  Raspberry_Pi_1 = Raspberry Pi 3 [part_number=RPI-3-V1.2]
  S1 = Momentary Switch [package=ksa_sealed_tac_switch]
  S2 = Momentary Switch [package=ksa_sealed_tac_switch]
  R9 = Resistor [tolerance=±5% resistance=10k package=THT]
  R10 = Resistor [tolerance=±5% resistance=10k package=THT]

nets:
  N1: LED4.cathode, LED1.cathode, LED5.cathode, LED6.cathode, Raspberry_Pi_1.GND, S1.4, S2.4
  N2: LED4.anode, R1.Pin_1
  N3: LED1.anode, R6.Pin_1
  N4: LED5.anode, R7.Pin_1
  N5: R1.Pin_0, Raspberry_Pi_1.GIPO18
  N6: R6.Pin_0, Raspberry_Pi_1.GIPO23
  N7: R7.Pin_0, Raspberry_Pi_1.GIPO24
  N8: R8.Pin_0, Raspberry_Pi_1.GIPO25
  N9: R8.Pin_1, LED6.anode
  3V3: Raspberry_Pi_1.3v3, Raspberry_Pi_1.3V3, S1.1, S2.1, R9.Pin_0, R10.Pin_0
  N10: Raspberry_Pi_1.GIPO7, R10.Pin_1
  N11: Raspberry_Pi_1.GIPO8, R9.Pin_1
