# Fritzing sketch 3주차 DTH-11 회로도 (saved by Fritzing 0.9.3b)
breadboards: 1

parts:
  Raspberry_Pi_1 = Raspberry Pi 3 [part_number=RPI-3-V1.2]
  Mod1 = KY-015 Temperature & Humidity Sensor Module [package="Breakout board"]

nets:
  N1: Raspberry_Pi_1.GIPO4, Mod1.S
  N2: Raspberry_Pi_1.GND, Mod1.-
  5V: Raspberry_Pi_1.5V, Mod1.Vin

custom parts:
  KY-015 Temperature & Humidity Sensor Module: KY-015 temperature and humidity sensor module, provides a low-latency serial interface to measure humidity and temperature.
