# Fritzing sketch 4주차 CdS 회로도 (saved by Fritzing 0.9.3b)
breadboards: 1

parts:
  Raspberry_Pi_1 = Raspberry Pi 3 [part_number=RPI-3-V1.2]
  LED1 = smd LED [color="Red (633nm)" package="0603 [SMD]"]
  R1 = Resistor [tolerance=±5% resistance=220 package="2512 [SMD]"]
  R2 = Resistor [tolerance=±5% resistance=220 package="2512 [SMD]"]
  R3 = PHOTOCELL [package=photocell]

nets:
  N1: Raspberry_Pi_1.3v3, R3.P$2
  N2: Raspberry_Pi_1.GPIO4, R2.Pin_0
  N3: Raspberry_Pi_1.GND, LED1.cathode, R2.Pin_1, R3.P$1
  N4: Raspberry_Pi_1.GPIO18, R1.Pin_1
  N5: LED1.anode, R1.Pin_0
