# Fritzing sketch SR04 (saved by Fritzing 0.9.3b)
breadboards: 1

parts:
  Raspberry_Pi_1 = Raspberry Pi 3 [part_number=RPI-3-V1.2]
  hc-sr1 = hc-sr04
  J1 = Piezo Speaker
  R1 = Resistor [tolerance=±5% resistance=2.2k package="0402 [SMD]"]
  R2 = Resistor [tolerance=±5% resistance=1k package="0402 [SMD]"]

nets:
  N1: Raspberry_Pi_1.GPIO25, hc-sr1.Echo, R2.Pin_0
  N2: Raspberry_Pi_1.GPIO24, hc-sr1.Trig, R1.Pin_0, R2.Pin_1
  N3: Raspberry_Pi_1.GPIO23, J1.pin2
  GND: Raspberry_Pi_1.GND, hc-sr1.GND, J1.pin1
  5V: Raspberry_Pi_1.5V, hc-sr1.VCC
