# Fritzing sketch 6주차 회로도 (saved by Fritzing 0.9.3b)
breadboards: 1

parts:
  R1 = Resistor [tolerance=±5% resistance=2.2k package=THT]
  Raspberry_Pi_1 = Raspberry Pi 3 [part_number=RPI-3-V1.2]
  LED1 = LED - 3mm [color="Red (633nm)" package="3 mm [THT]"]

nets:
  N1: R1.Pin_1, Raspberry_Pi_1.GND, LED1.cathode
  N2: Raspberry_Pi_1.GIPO18, LED1.anode
